# Fritzing sketch ElbanquosKitchentimer_MK2 (saved by Fritzing 0.9.3b)
breadboards: 5

parts:
  S1 = Pushbutton [package="[THT]"]
  S2 = Pushbutton [package="[THT]"]
  S3 = Pushbutton [package="[THT]"]
  S4 = Pushbutton [package="[THT]"]
  LED1 = smd LED [color="Red (633nm)" package="1206 [SMD]"]
  LED2 = smd LED [color="Red (633nm)" package="1206 [SMD]"]
  LED3 = smd LED [color="Red (633nm)" package="1206 [SMD]"]
  LED4 = smd LED [color="Red (633nm)" package="1206 [SMD]"]
  RE1 = Rotary Encoder [package=THT]
  Rotary_Button_Function = Pushbutton [package="[THT]"]
  J1 = Piezo Speaker
  R1 = Resistor [tolerance=±5% resistance=560 package=THT]
  R3 = Resistor [tolerance=±5% resistance=4.7k package=THT]
  Power_Adapter = Power plug
  The_Nano = Arduino Nano (Rev3.0)
  R2 = Trimmer Potentiometer [maximum_resistance=100kΩ package=THT]
  Q1 = NPN-Transistor [package="TO92 [THT]"]
  J2 = Camdenboss CTB0158-4 [part_number=CTB0158-4 package=THT]
  C1 = Ceramic Capacitor [capacitance=100nF package="100 mil [THT, multilayer]"]
  U1 = 74HC595 [package="DIP16 [THT]"]
  LED7 = smd LED [color="Green (555nm)" package="1206 [SMD]"]
  LED8 = smd LED [color="Green (555nm)" package="1206 [SMD]"]
  LED9 = smd LED [color="Green (555nm)" package="1206 [SMD]"]
  LED10 = smd LED [color="Green (555nm)" package="1206 [SMD]"]
  R4 = Resistor [tolerance=±10% resistance=220 package="2010 [SMD]"]
  R5 = Resistor [tolerance=±10% resistance=220 package="2010 [SMD]"]
  R6 = Resistor [tolerance=±10% resistance=220 package="2010 [SMD]"]
  R7 = Resistor [tolerance=±10% resistance=220 package="2010 [SMD]"]
  U3 = MAX7219 [package=dil24]  # not connected
  7_Segment1 = 7 Segment Display  # not connected
  7_Segment2 = 7 Segment Display  # not connected
  7_Segment3 = 7 Segment Display  # not connected
  7_Segment4 = 7 Segment Display  # not connected
  7_Segment5 = 7 Segment Display  # not connected
  7_Segment6 = 7 Segment Display  # not connected
  7_Segment7 = 7 Segment Display  # not connected
  7_Segment8 = 7 Segment Display  # not connected
  R8 = Resistor [tolerance=±5% resistance=22k package=THT]
  R9 = Resistor [tolerance=±5% resistance=22k package=THT]
  R10 = Resistor [tolerance=±5% resistance=22k package=THT]
  R11 = Resistor [tolerance=±5% resistance=22k package=THT]

nets:
  N1: S1.Pin_3, The_Nano.A2, R9.Pin_1
  N2: S2.Pin_1, S2.Pin_2, The_Nano.A4, R11.Pin_1
  5V: S2.Pin_3, S2.Pin_4, The_Nano.5V, U1.MR, U1.VCC
  N3: S3.Pin_3, The_Nano.A3, R10.Pin_1
  N4: S4.Pin_3, The_Nano.A1, R8.Pin_1
  N5: LED1.cathode, U1.Q7, LED9.anode
  N6: LED1.anode, LED9.cathode, R5.Pin_0
  N7: LED2.cathode, U1.Q1, LED7.anode
  N8: LED2.anode, LED7.cathode, R4.Pin_0
  N9: LED3.cathode, U1.Q3, LED8.anode
  N10: LED3.anode, LED8.cathode, R7.Pin_0
  N11: LED4.cathode, U1.Q5, LED10.anode
  N12: LED4.anode, LED10.cathode, R6.Pin_0
  N13: RE1.EncoderPinA, The_Nano.D11/MOSI
  GND: RE1.EncoderPinC, Rotary_Button_Function.Pin_3, Rotary_Button_Function.Pin_4, J1.pin1, R1.Pin_1, R3.Pin_1, Power_Adapter.GND, The_Nano.GND, J2.pin2, C1.1, U1.GND, U1.OE, R8.Pin_0, R9.Pin_0, R10.Pin_0, R11.Pin_0
  N14: RE1.EncoderPinB, The_Nano.D10
  N15: Rotary_Button_Function.Pin_1, Rotary_Button_Function.Pin_2, The_Nano.D12/MISO
  N16: J1.pin2, R3.Pin_0, Q1.E
  N17: R1.Pin_0, R2.leg1
  VCC: Power_Adapter.VCC, The_Nano.VIN, Q1.C, J2.pin3, J2.pin4, C1.0
  N18: The_Nano.D2, U1.ST_CP
  N19: The_Nano.D3, U1.SH_CP
  N20: The_Nano.D4, U1.DS
  N21: The_Nano.D5, R2.leg2
  N22: R2.wiper, Q1.B
  N23: U1.Q2, R7.Pin_1
  N24: U1.Q4, R6.Pin_1
  N25: U1.Q6, R5.Pin_1
  N26: U1.Q0, R4.Pin_1

notes:
  Some Magic here->
